// Logisim project MYCPU.circ as structural Verilog: 5 circuits, main circuit MyCpu
// reset
module MyCpu (
);

  wire alu_1_negaticve, alu_1_out_10, alu_1_zero, and_1_out, and_2_out, and_3_out, clk_out, nor_1_out,
       not_1_out, not_2_out, or_1_out, reset_out, unit_control_1_halt, unit_control_1_load,
       unit_control_1_out_2, unit_control_1_power_jump, unit_control_1_set_flag, unit_control_1_store,
       unit_control_1_write_back;
  wire [15:0] adder_1_out, alu_1_result, multiplexer_1_out, multiplexer_2_out, multiplexer_3_out,
       multiplexer_4_out, program_counter_q, ram_1_data, ram_2_data, register_file_1_out_6,
       register_file_1_out_7, register_file_1_out_8, register_file_1_out_9, register_file_1_reg1_output,
       register_file_1_reg2_output, sign_extention_1_out_2;

  Register #(.width(16)) program_counter (
    .D(multiplexer_1_out), .en(unit_control_1_halt), .Q(program_counter_q), .clk(clk_out), .clr(reset_out));
  Button reset (.out(reset_out));
  Clock clk (.out(clk_out));
  // Probe on register_file_1_out_9
  Adder #(.width(16)) adder_1 (.a(program_counter_q), .b(16'h1), .out(adder_1_out));  // open: cin, cout
  Multiplexer #(.width(16), .enable("false")) multiplexer_1 (
    .in0(adder_1_out), .in1(multiplexer_3_out), .out(multiplexer_1_out), .sel(and_1_out));
  RAM #(.addrWidth(16), .dataWidth(16), .bus("separate")) ram_1 (
    .addr(program_counter_q), .data(ram_1_data), .ld(1'b1));  // open: din, str, sel, clk, clr
  // Probe on register_file_1_out_8
  // Probe on register_file_1_out_7
  // Probe on register_file_1_out_6
  REGISTER_FILE register_file_1 (
    .WRITE(and_2_out), .REG1(ram_1_data[9:8]), .REG2(ram_1_data[11:10]), .DATA_INPUT(multiplexer_2_out),
    .CLK(clk_out), .out_9(register_file_1_out_9), .out_8(register_file_1_out_8),
    .out_7(register_file_1_out_7), .out_6(register_file_1_out_6), .REG1_OUTPUT(register_file_1_reg1_output),
    .REG2_OUTPUT(register_file_1_reg2_output));
  Sign_Extention sign_extention_1 (.in_1(ram_1_data[7:0]), .out_2(sign_extention_1_out_2));
  and and_1 (and_1_out, nor_1_out, unit_control_1_power_jump);
  Multiplexer #(.width(16), .enable("false")) multiplexer_2 (
    .in0(alu_1_result), .in1(ram_2_data), .out(multiplexer_2_out), .sel(unit_control_1_load));
  UNIT_CONTROL unit_control_1 (
    .out_2(unit_control_1_out_2), .set_flag(unit_control_1_set_flag), .write_back(unit_control_1_write_back),
    .power_jump(unit_control_1_power_jump), .load(unit_control_1_load), .store(unit_control_1_store),
    .halt(unit_control_1_halt), .DASTOOR(ram_1_data));
  Multiplexer #(.width(16), .enable("false")) multiplexer_3 (
    .in0(register_file_1_reg2_output), .in1(sign_extention_1_out_2), .out(multiplexer_3_out),
    .sel(unit_control_1_out_2));
  and and_2 (and_2_out, ~clk_out, or_1_out);  // AND_Gate
  LED ZF (.in(alu_1_zero));
  LED NF (.in(alu_1_negaticve));
  nor nor_1 (nor_1_out, alu_1_zero, alu_1_negaticve);
  ALU alu_1 (
    .input1__alu(register_file_1_reg1_output), .input2_alu(multiplexer_3_out), .in_4(clk_out),
    .in_6(unit_control_1_write_back), .RESULT(alu_1_result), .out_10(alu_1_out_10),
    .op__alu(ram_1_data[14:12]), .in_5(and_3_out), .ZERO(alu_1_zero), .NEGATICVE(alu_1_negaticve));
  or or_1 (or_1_out, unit_control_1_load, alu_1_out_10);
  Multiplexer #(.width(16), .enable("false")) multiplexer_4 (
    .in0(register_file_1_reg1_output), .in1(register_file_1_reg2_output), .out(multiplexer_4_out),
    .sel(not_1_out));
  not not_1 (not_1_out, unit_control_1_store);
  not not_2 (not_2_out, clk_out);
  buf and_3 (and_3_out, unit_control_1_set_flag);  // AND_Gate
  RAM #(.addrWidth(16), .dataWidth(16), .bus("separate")) ram_2 (
    .addr(multiplexer_4_out), .din(register_file_1_reg2_output), .data(ram_2_data),
    .str(unit_control_1_store), .clk(not_2_out), .ld(1'b1));  // open: sel, clr

  // Notes on the sheet:
  //                                            RAM
  //          op2
  //   op1     
endmodule

module ALU (
  input  [15:0] input1__alu,
  input  [15:0] input2_alu,
  input  [2:0] op__alu,
  input  in_4,
  input  in_5,
  input  in_6,
  output [15:0] RESULT,
  output NEGATICVE,
  output ZERO,
  output out_10
);

  wire nor_1_out, not_1_out;
  wire [15:0] adder_1_out, multiplier_1_out, or_1_out, subtractor_1_out, xor_1_out;

  not not_1 (not_1_out, in_4);
  Adder #(.width(16)) adder_1 (.a(input1__alu), .b(input2_alu), .out(adder_1_out));  // open: cin, cout
  Subtractor #(.width(16)) subtractor_1 (.a(input1__alu), .b(input2_alu), .out(subtractor_1_out));  // open: bin, bout
  Multiplier #(.width(16)) multiplier_1 (.a(input1__alu), .b(input2_alu), .out(multiplier_1_out));  // open: cin, cout
  assign xor_1_out = input1__alu ^ input2_alu;  // XOR_Gate xor_1, 16 bits wide
  assign or_1_out = {16{1'b0}} | input2_alu;  // OR_Gate or_1, 16 bits wide
  and and_1 (out_10, not_1_out, in_6);
  Multiplexer #(.select(3), .width(16), .enable("false")) multiplexer_1 (
    .in0(adder_1_out), .in1(subtractor_1_out), .in2(multiplier_1_out), .in3(xor_1_out), .in4(or_1_out),
    .in5({16{1'b0}}), .in6({16{1'b0}}), .in7({16{1'b0}}), .out(RESULT), .sel(op__alu));
  nor nor_1 (nor_1_out, RESULT[15], RESULT[14], RESULT[13], RESULT[12], RESULT[11], RESULT[10], RESULT[9], RESULT[8], RESULT[7], RESULT[6], RESULT[5], RESULT[4], RESULT[3], RESULT[2], RESULT[1], RESULT[0]);
  Register #(.width(1)) u_ZERO (.D(nor_1_out), .Q(ZERO), .clk(in_5));  // open: en, clr
  Register #(.width(1)) NEGATIVE (.D(RESULT[15]), .Q(NEGATICVE), .clk(in_5));  // open: en, clr
endmodule

// register_file
module REGISTER_FILE (
  input  WRITE,
  input  [1:0] REG1,
  input  [1:0] REG2,
  input  [15:0] DATA_INPUT,
  input  CLK,
  output [15:0] out_6,
  output [15:0] out_7,
  output [15:0] out_8,
  output [15:0] out_9,
  output [15:0] REG1_OUTPUT,
  output [15:0] REG2_OUTPUT
);

  wire and_1_out, and_2_out, and_3_out, and_4_out, decoder_1_out0, decoder_1_out1, decoder_1_out2,
       decoder_1_out3;

  Decoder #(.select(2), .enable("false")) decoder_1 (
    .out0(decoder_1_out0), .out1(decoder_1_out1), .out2(decoder_1_out2), .out3(decoder_1_out3), .sel(REG1));
  and and_1 (and_1_out, decoder_1_out0, WRITE);
  and and_2 (and_2_out, decoder_1_out1, WRITE);
  and and_3 (and_3_out, decoder_1_out2, WRITE);
  and and_4 (and_4_out, decoder_1_out3, WRITE);
  Register #(.width(16)) register_1 (.D(DATA_INPUT), .en(and_1_out), .Q(out_9), .clk(CLK), .clr(1'b0));
  Register #(.width(16)) register_2 (.D(DATA_INPUT), .en(and_2_out), .Q(out_8), .clk(CLK), .clr(1'b0));
  Register #(.width(16)) register_3 (.D(DATA_INPUT), .en(and_3_out), .Q(out_7), .clk(CLK), .clr(1'b0));
  Register #(.width(16)) register_4 (.D(DATA_INPUT), .en(and_4_out), .Q(out_6), .clk(CLK), .clr(1'b0));
  Multiplexer #(.select(2), .width(16), .enable("false")) multiplexer_1 (
    .in0(out_9), .in1(out_8), .in2(out_7), .in3(out_6), .out(REG1_OUTPUT), .sel(REG1));
  Multiplexer #(.select(2), .width(16), .enable("false")) multiplexer_2 (
    .in0(out_9), .in1(out_8), .in2(out_7), .in3(out_6), .out(REG2_OUTPUT), .sel(REG2));
endmodule

module UNIT_CONTROL (
  input  [15:0] DASTOOR,
  output out_2,
  output set_flag,
  output write_back,
  output power_jump,
  output load,
  output store,
  output halt
);

  wire and_1_out, and_5_out;

  and and_1 (and_1_out, ~DASTOOR[15], ~DASTOOR[14]);  // AND_Gate
  and and_2 (power_jump, ~DASTOOR[15], DASTOOR[14], DASTOOR[13], DASTOOR[12]);  // AND_Gate
  and and_3 (load, ~DASTOOR[15], ~DASTOOR[13], DASTOOR[14], DASTOOR[12]);  // AND_Gate
  and and_4 (store, ~DASTOOR[15], ~DASTOOR[12], DASTOOR[14], DASTOOR[13]);  // AND_Gate
  nand nand_1 (halt, DASTOOR[12], DASTOOR[13], DASTOOR[14], DASTOOR[15]);
  nand nand_2 (set_flag, ~DASTOOR[15], DASTOOR[14], DASTOOR[13]);  // NAND_Gate
  and and_5 (and_5_out, ~DASTOOR[13], ~DASTOOR[13]);  // AND_Gate
  nand nand_3 (out_2, DASTOOR[0], DASTOOR[1], DASTOOR[2], DASTOOR[3], DASTOOR[5], DASTOOR[6], DASTOOR[7]);
  or or_1 (write_back, and_1_out, and_5_out);
endmodule

// Sign Ext
module Sign_Extention (
  input  [7:0] in_1,
  output [15:0] out_2
);


  assign out_2 = {{9{in_1[7]}}, in_1[6:0]};
endmodule
